# Fritzing sketch OLOwiring (saved by Fritzing 0.9.2b)

parts:
  WeMos_D1_Mini1 = WeMos D1 Mini
  HLK-PM1 = HLK-PM01
  J1 = Generic male header - 4 pins [form="♂ (male)" package=THT]
  U1 = POT [package=pot_mammoth]
  LED1 = LEDs [package=led10mm]
  J2 = female pin header, 2 pins [form="♀ (female)"]

nets:
  3V3: WeMos_D1_Mini1.3V3, J1.VCC, U1.E
  N1: WeMos_D1_Mini1.5V, HLK-PM1.-Vo
  N2: WeMos_D1_Mini1.A0, U1.A
  N3: WeMos_D1_Mini1.D1, J1.PWM
  N4: WeMos_D1_Mini1.D2, J1.Z-C
  N5: WeMos_D1_Mini1.G, HLK-PM1.+Vo, J1.GND, U1.S
  N6: HLK-PM1.AC#0, J1.L-_IN, J2.pin1
  N7: HLK-PM1.AC#1, J1.N#6, J2.pin2
  N8: J1.L-_OUT, LED1.A
  N9: J1.N#7, LED1.C

notes:
  220V plug
  (polarity doesn't matter)

custom parts:
  WeMos D1 Mini: The D1 mini is a mini wifi board based on ESP-8266EX.
  Generic male header - 4 pins: Generic male header
  LEDs: LEDs Standard schematic elements and footprints for 5mm, 3mm, 1206, and 0603 sized LEDs. 5mm - Spark Fun Electronics SKU : COM-00529 (and others)
